# Fritzing sketch Pilarm (saved by Fritzing 0.9.2b)
breadboards: 1

parts:
  Raspberry_Pi1 = Raspberry Pi B+
  SW1 = PowerSwitch Tail II
  PIR1 = PIR sensor
  KEYPAD1 = Membrane Matrix Keypad
  AMP1 = MAX98306_Stereo_Amplifier
  U1 = AUDIO-JACK2 [package=audio-jack-3.5mm-smd]
  BATT1 = 4xAA Switchable Battery Pack w/Bare Wire
  SP1 = SPEAKER [package=pcb_mount_speaker]
  LED1 = LEDs [package=led10mm]
  LED2 = LEDs [package=led10mm]
  R1 = Resistor [tolerance=±5% resistance=220 package="0805 [SMD]"]
  R2 = Resistor [tolerance=±5% resistance=220 package="0805 [SMD]"]
  Pi1 = Adafruit Pi Cobbler
  J1 = Cobbler Plus Cable

nets:
  3V3: Raspberry_Pi1.3v3, Raspberry_Pi1.3V3, J1.3.3V#41, J1.3.3V#57
  N1: Raspberry_Pi1.GPIO2, J1.GPIO_2
  N2: Raspberry_Pi1.GPIO3, J1.GPIO_3
  N3: Raspberry_Pi1.GIPO4, J1.GPIO_4
  N4: Raspberry_Pi1.GND, J1.GND#46, J1.GND#49, J1.GND#54, J1.GND#60, J1.GND#65, J1.GND#70, J1.GND#74, J1.GND#79
  N5: Raspberry_Pi1.GIPO17, J1.GPIO_17
  N6: Raspberry_Pi1.GIPO27, J1.GPIO_27
  N7: Raspberry_Pi1.GIPO22, J1.GPIO_22
  N8: Raspberry_Pi1.GIPO10, J1.GPIO_10
  N9: Raspberry_Pi1.GIPO9, J1.GPIO_9
  N10: Raspberry_Pi1.GIPO11, J1.GPIO_11
  N11: Raspberry_Pi1.ID_SD, J1.ID_SD
  N12: Raspberry_Pi1.GIPO5, J1.GPIO_5
  N13: Raspberry_Pi1.GIPO6, J1.GPIO_6
  N14: Raspberry_Pi1.GIPO13, J1.GPIO_13
  N15: Raspberry_Pi1.GIPO19, J1.GPIO_19
  N16: Raspberry_Pi1.GIPO26, J1.GPIO_26
  N17: Raspberry_Pi1.GIPO21, J1.GPIO_21
  N18: Raspberry_Pi1.GIPO20, J1.GPIO_20
  N19: Raspberry_Pi1.GIPO16, J1.GPIO_16
  N20: Raspberry_Pi1.GIPO12, J1.GPIO_12
  N21: Raspberry_Pi1.ID_SC, J1.ID_SC
  N22: Raspberry_Pi1.GIPO7, J1.GPIO_7
  N23: Raspberry_Pi1.GIPO8, J1.GPIO_8
  N24: Raspberry_Pi1.GIPO25, J1.GPIO_25
  N25: Raspberry_Pi1.GIPO24, J1.GPIO_24
  N26: Raspberry_Pi1.GIPO23, J1.GPIO_23
  N27: Raspberry_Pi1.GIPO18, J1.GPIO_18
  N28: Raspberry_Pi1.GIPO15, J1.GPIO_15
  N29: Raspberry_Pi1.GIPO14, J1.GPIO_14
  5V: Raspberry_Pi1.5V, J1.5V
  N30: SW1.+in, Pi1.MOSI, J1.MOSI
  N31: SW1.-in, PIR1.GND, Pi1.PIN25, J1.GND#24
  3V3_2: PIR1.VDD, Pi1.3V3, J1.3V3
  N32: PIR1.SIG, Pi1.#22, J1.#22
  N33: KEYPAD1.1, Pi1.#18, J1.#18
  N34: KEYPAD1.2, Pi1.#23, J1.#23
  N35: KEYPAD1.3, Pi1.#24, J1.#24
  N36: KEYPAD1.4, Pi1.#25, J1.#25
  N37: KEYPAD1.5, Pi1.#4, J1.#4
  N38: KEYPAD1.6, Pi1.#17, J1.#17
  N39: KEYPAD1.7, Pi1.#21, J1.#27
  N40: AMP1.connector1, BATT1.POS
  N41: AMP1.connector2, BATT1.NEG
  N42: AMP1.connector4, U1.RSH
  N43: AMP1.connector6, U1.TIP
  N44: AMP1.connector7, U1.TSH
  N45: AMP1.connector12, SP1.+
  N46: AMP1.connector13, SP1.-
  N47: LED1.A, R1.Pin_1
  N48: LED1.C, LED2.C, Pi1.GND, J1.GND#5
  N49: LED2.A, R2.Pin_1
  N50: R1.Pin_0, Pi1.RXD, J1.RXD
  N51: R2.Pin_0, Pi1.TXD, J1.TXD
  N52: Pi1.5V0, J1.5.0V#1
  N53: Pi1.SDA0, J1.SDA
  N54: Pi1.PIN4, J1.5.0V#3
  N55: Pi1.SCL0, J1.SCL
  N56: Pi1.PIN9, J1.GND#8
  N57: Pi1.PIN14, J1.GND#13
  N58: Pi1.PIN19, J1.3.3V#16
  N59: Pi1.PIN20, J1.GND#19
  N60: Pi1.MISO, J1.MISO
  N61: Pi1.SCLK, J1.SCLK
  N62: Pi1.CE0, J1.CE0
  N63: Pi1.CE1, J1.CE1

notes:
  PowerSwitch gets plugged into the flashing light.
  You don't need a breakout board for the cable here, you can just cut an 1/8" audio cable and wire it directly to the audio amp. This breakout here is just for illustration.

custom parts:
  Raspberry Pi B+: The awesome Raspberry Pi ARM Board with 40 pin gipo. Ready for special designed Raspberry Pi B+ Hat (Hardware attached (on) top)
  Membrane Matrix Keypad: Membrane Matrix 3x4 Keypad
  4xAA Switchable Battery Pack w/Bare Wire: 4xAA Switchable Battery Pack with Bare Wire connection
  Adafruit Pi Cobbler: Adafruit Pi Cobbler GPIO Breakout for Raspberry Pi
  Cobbler Plus Cable: The Cobbler Plus is an add on prototyping board from Adafruit specifically designed for the Raspberry Pi B+ that can break out all those tasty power, GPIO, I2C and SPI pins from the 40-pin header onto a solderless breadboard. This set will make "cobbling together" prototypes with the Pi super easy. The Cobbler Plus can plug into any solderless breadboard.
